// Digital circuit Punto1_Multiplexor_8_entradas.dig as structural Verilog
module Punto1_Multiplexor_8_entradas (
  input  D0,
  input  D1,
  input  D2,
  input  D3,
  input  D4,
  input  D5,
  input  D6,
  input  Sel2,
  input  Sel1,
  input  Sel0,
  input  D7,
  output Output
);

  wire and_1_out, and_2_out, and_3_out, and_4_out, and_5_out, and_6_out, and_7_out, and_8_out, not_1_out,
       not_2_out, not_3_out, or_1_out, or_2_out;

  not not_1 (not_1_out, Sel2);
  not not_2 (not_2_out, Sel1);
  not not_3 (not_3_out, Sel0);
  and and_1 (and_1_out, D0, not_3_out, not_2_out, not_1_out);
  and and_2 (and_2_out, D1, Sel0, not_2_out, not_1_out);
  and and_3 (and_3_out, D2, Sel1, not_3_out, not_1_out);
  and and_4 (and_4_out, D3, Sel1, Sel0, not_1_out);
  and and_5 (and_5_out, D4, Sel2, not_3_out, not_2_out);
  and and_6 (and_6_out, D5, Sel2, Sel0, not_2_out);
  and and_7 (and_7_out, D6, Sel2, Sel1, not_3_out);
  and and_8 (and_8_out, D7, Sel2, Sel1, Sel0);
  or or_1 (or_1_out, and_1_out, and_2_out, and_3_out, and_4_out);
  or or_2 (or_2_out, and_5_out, and_6_out, and_7_out, and_8_out);
  or or_3 (Output, or_1_out, or_2_out);
endmodule
