// Digital circuit Punto2_Demultiplexor.dig as structural Verilog
module Punto2_Demultiplexor (
  input  Sel1,
  input  Sel0,
  input  Entrada,
  output S0,
  output S1,
  output S2,
  output S3
);

  wire not_1_out, not_2_out;

  not not_1 (not_1_out, Sel1);
  not not_2 (not_2_out, Sel0);
  and and_1 (S0, Entrada, not_2_out, not_1_out);
  and and_2 (S1, Entrada, Sel0, not_1_out);
  and and_3 (S2, Entrada, Sel1, not_2_out);
  and and_4 (S3, Entrada, Sel0, Sel1);
endmodule
