// Digital circuit Punto3_flipflopJK.dig as structural Verilog
module Punto3_flipflopJK (
  input  J,
  input  Clock,
  input  K,
  output Q,
  output Q_2
);

  wire nand_1_out, nand_2_out, nand_3_out, nand_4_out, nand_5_out, nand_6_out, nand_7_out, nand_8_out,
       nand_9_out, nand_10_out, not_1_out, not_2_out;

  not not_1 (not_1_out, Clock);
  nand nand_1 (nand_1_out, Q_2, J);
  nand nand_2 (nand_2_out, K, Q);
  nand nand_3 (nand_3_out, nand_1_out, nand_1_out);
  nand nand_4 (nand_4_out, nand_2_out, nand_2_out);
  not not_2 (not_2_out, not_1_out);
  nand nand_5 (nand_5_out, nand_3_out, not_1_out);
  nand nand_6 (nand_6_out, not_1_out, nand_4_out);
  nand nand_7 (nand_7_out, nand_5_out, nand_8_out);
  nand nand_8 (nand_8_out, nand_7_out, nand_6_out);
  nand nand_9 (nand_9_out, nand_7_out, not_2_out);
  nand nand_10 (nand_10_out, not_2_out, nand_8_out);
  nand nand_11 (Q, nand_9_out, Q_2);
  nand nand_12 (Q_2, Q, nand_10_out);

  // Notes on the sheet:
  //   El funcionamiento del flipflop JK es en esencia el mismo del flipflop SR, sin embargo 
  //   tiene una diferencia muy importante en la forma en la cual se almacenan los datos,
  //   gracias a que el dato de salida está conectado a la entrada inversa, se logra eliminar 
  //   la oscilacion que se presentaba en el flipflop SR. De esta forma, cuando se activa el clock 
  //   mientras que las entradas J y K estan encendidas, se puede observar que en cada flanco de 
  //   subida la salida cambia entre Q y Q'
endmodule
