// Digital circuit Punto3_flipflopSR.dig as structural Verilog
module Punto3_flipflopSR (
  input  S,
  input  R,
  input  Clock,
  output Q,
  output Q_2
);

  wire nand_1_out, nand_2_out, nand_3_out, nand_4_out, nand_5_out, nand_6_out, not_1_out, not_2_out;

  not not_1 (not_1_out, Clock);
  nand nand_1 (nand_1_out, S, not_1_out);
  not not_2 (not_2_out, not_1_out);
  nand nand_2 (nand_2_out, not_1_out, R);
  nand nand_3 (nand_3_out, nand_1_out, nand_4_out);
  nand nand_4 (nand_4_out, nand_3_out, nand_2_out);
  nand nand_5 (nand_5_out, nand_3_out, not_2_out);
  nand nand_6 (nand_6_out, not_2_out, nand_4_out);
  nand nand_7 (Q, nand_5_out, Q_2);
  nand nand_8 (Q_2, Q, nand_6_out);

  // Notes on the sheet:
  //   El flipflop SR se usa para almacenar un dato, funciona gracias al flanco de subida del clock.
  //   Primero, se enciende una de las dos entradas (S o R) mientras el Clock está en 0, de esta forma se guarda el 
  //   estado en la parte del maestro y luego al encender el clock pasa habilita el esclavo y se deshabilita el maestro 
  //   de esta forma la señal de entrada es trasladada del maestro al esclavo y se muestra en la salida correspondiente.
  //   Es importante destacar, que cuando se trata de activar el Clock con ambas entradas encendidas, se presenta un 
  //   estado de oscilacion generando asi un error indeseado.
endmodule
