// Digital circuit Punto4_PIN.dig as structural Verilog
module Punto4_PIN (
  input  Enable,
  input  Clear,
  input  Set,
  input  in_4,
  input  in_5,
  input  in_6,
  input  in_7,
  input  Dato_S1,
  input  Dato_S2,
  input  Dato_S3,
  input  Dato_S4,
  input  Enable2,
  input  clk,
  input  E1,
  input  E2,
  input  E3,
  input  E4,
  output Guardado1,
  output Guardado2,
  output Guardado3,
  output Guardado4,
  output S1,
  output S2,
  output S3,
  output S4
);

  wire d_ff_as_4_q, d_ff_as_6_q, d_ff_as_7_q, d_ff_as_9_q, E1_t, E2_t, E3_t, E4_t, multiplexer_1_out,
       multiplexer_2_out, multiplexer_3_out, multiplexer_4_out, multiplexer_5_out, multiplexer_6_out,
       multiplexer_7_out, multiplexer_8_out, multiplexer_9_out, multiplexer_10_out, multiplexer_11_out,
       multiplexer_12_out, S1_t, S2_t, S3_t, S4_t;

  PullDown pulldown_1 (.out(E1_t));
  Multiplexer multiplexer_1 (.sel(Enable2), .in_0(Guardado1), .in_1(E1_t), .out(multiplexer_1_out));
  D_FF_AS d_ff_as_1 (.Set(Set), .D(multiplexer_1_out), .C(clk), .Clr(Clear), .Q(Guardado1));  // open: nQ
  PullDown pulldown_2 (.out(E2_t));
  Multiplexer multiplexer_2 (.sel(Enable2), .in_0(Guardado2), .in_1(E2_t), .out(multiplexer_2_out));
  D_FF_AS d_ff_as_2 (.Set(Set), .D(multiplexer_2_out), .C(clk), .Clr(Clear), .Q(Guardado2));  // open: nQ
  PullDown pulldown_3 (.out(E3_t));
  Multiplexer multiplexer_3 (.sel(Enable2), .in_0(Guardado3), .in_1(E3_t), .out(multiplexer_3_out));
  Multiplexer multiplexer_4 (.sel(Enable), .in_0(d_ff_as_4_q), .in_1(in_4), .out(multiplexer_4_out));
  D_FF_AS d_ff_as_3 (.Set(Set), .D(multiplexer_3_out), .C(clk), .Clr(Clear), .Q(Guardado3));  // open: nQ
  PullDown pulldown_4 (.out(E4_t));
  D_FF_AS d_ff_as_4 (.Set(Set), .D(multiplexer_4_out), .C(clk), .Clr(Clear), .Q(d_ff_as_4_q));  // open: nQ
  assign E1_t = d_ff_as_4_q ? E1 : 1'bz;  // Driver driver_1
  Multiplexer multiplexer_5 (.sel(Enable2), .in_0(Guardado4), .in_1(E4_t), .out(multiplexer_5_out));
  Multiplexer multiplexer_6 (.sel(Enable), .in_0(d_ff_as_6_q), .in_1(in_5), .out(multiplexer_6_out));
  assign S1 = ~d_ff_as_4_q ? S1_t : 1'bz;  // DriverInvSel driverinvsel_1
  D_FF_AS d_ff_as_5 (.Set(Set), .D(multiplexer_5_out), .C(clk), .Clr(Clear), .Q(Guardado4));  // open: nQ
  D_FF_AS d_ff_as_6 (.Set(Set), .D(multiplexer_6_out), .C(clk), .Clr(Clear), .Q(d_ff_as_6_q));  // open: nQ
  assign E2_t = d_ff_as_6_q ? E2 : 1'bz;  // Driver driver_2
  Multiplexer multiplexer_7 (.sel(Enable), .in_0(d_ff_as_7_q), .in_1(in_6), .out(multiplexer_7_out));
  assign S2 = ~d_ff_as_6_q ? S2_t : 1'bz;  // DriverInvSel driverinvsel_2
  D_FF_AS d_ff_as_7 (.Set(Set), .D(multiplexer_7_out), .C(clk), .Clr(Clear), .Q(d_ff_as_7_q));  // open: nQ
  Multiplexer multiplexer_8 (.sel(Enable2), .in_0(S1_t), .in_1(Dato_S1), .out(multiplexer_8_out));
  assign E3_t = d_ff_as_7_q ? E3 : 1'bz;  // Driver driver_3
  D_FF_AS d_ff_as_8 (.Set(Set), .D(multiplexer_8_out), .C(clk), .Clr(Clear), .Q(S1_t));  // open: nQ
  Multiplexer multiplexer_9 (.sel(Enable), .in_0(d_ff_as_9_q), .in_1(in_7), .out(multiplexer_9_out));
  assign S3 = ~d_ff_as_7_q ? S3_t : 1'bz;  // DriverInvSel driverinvsel_3
  Multiplexer multiplexer_10 (.sel(Enable2), .in_0(S2_t), .in_1(Dato_S2), .out(multiplexer_10_out));
  D_FF_AS d_ff_as_9 (.Set(Set), .D(multiplexer_9_out), .C(clk), .Clr(Clear), .Q(d_ff_as_9_q));  // open: nQ
  D_FF_AS d_ff_as_10 (.Set(Set), .D(multiplexer_10_out), .C(clk), .Clr(Clear), .Q(S2_t));  // open: nQ
  assign E4_t = d_ff_as_9_q ? E4 : 1'bz;  // Driver driver_4
  Multiplexer multiplexer_11 (.sel(Enable2), .in_0(S3_t), .in_1(Dato_S3), .out(multiplexer_11_out));
  assign S4 = ~d_ff_as_9_q ? S4_t : 1'bz;  // DriverInvSel driverinvsel_4
  D_FF_AS d_ff_as_11 (.Set(Set), .D(multiplexer_11_out), .C(clk), .Clr(Clear), .Q(S3_t));  // open: nQ
  Multiplexer multiplexer_12 (.sel(Enable2), .in_0(S4_t), .in_1(Dato_S4), .out(multiplexer_12_out));
  D_FF_AS d_ff_as_12 (.Set(Set), .D(multiplexer_12_out), .C(clk), .Clr(Clear), .Q(S4_t));  // open: nQ

  // Other names for the same wires on the sheet: Clock = clk

  // Notes on the sheet:
  //   clk: Hz: 10
  //   Registro de Entrada
  //   - Con el registro de configuracion se selecciona si se activa el registro de entrada o el de salida.
  //   (siempre y cuando esté activado el Enable).
  //   1 para activar el registro de Entrada.
  //   0 para activar el registro de Salida.
  //   - El registro de Entrada tomará el valor de entrada del pin y lo guardará en su lugar respectivo
  //   del registro de entrada (siempre y cuando esté activado el Enable2).
  //   - El registro de Salida enseñara en el pin respectivo el dato asignado en las entradas del registro de 
  //   salida (siempre y cuando esté activado el Enable2).
  //   Pin1
  //   Registro de Configuración
  //   Pin2
  //   Pin3
  //   Registro de Salida
  //   Pin4
endmodule
